# Fritzing sketch fritzing_diagram (saved by Fritzing 0.9.4)

parts:
  Mod1 = Arduino Uno WIFI REV2
  LCD2004-I2C1 = LCD2004-I2C

nets:
  5V: Mod1.5V, LCD2004-I2C1.VCC
  GND: Mod1.GND, LCD2004-I2C1.GND
  N1: Mod1.A4/SDA, LCD2004-I2C1.SDA
  N2: Mod1.A5/SCL, LCD2004-I2C1.SCL

custom parts:
  Arduino Uno WIFI REV2: The Arduino Uno WIFI REV2 is a microcontroller board based on the ATmega 4809. It has 14 digital input/output pins (of which 5 can be used as PWM outputs), 6 analog inputs, a 16 MHz ceramic resonator, a USB connection, a power jack, an ICSP header, and a reset button. It also has a WIFI controller with a secure ECC608 crypto unit and an internal IMU. It contains everything needed to support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
  LCD2004-I2C: A standard character display with 4x20 characters. Comes in many colors with LCM2004 IIC attached.
